# Fritzing sketch zspod (saved by Fritzing 0.9.3b)
circuit board: 9.99578cm x 6.95982cm
breadboards: 1

parts:
  m+ = Momentary Switch [package=ksa_sealed_tac_switch]
  m- = Momentary Switch [package=ksa_sealed_tac_switch]
  h+ = Momentary Switch [package=ksa_sealed_tac_switch]
  h- = Momentary Switch [package=ksa_sealed_tac_switch]
  D+ = Momentary Switch [package=ksa_sealed_tac_switch]
  D- = Momentary Switch [package=ksa_sealed_tac_switch]
  M- = Momentary Switch [package=ksa_sealed_tac_switch]
  Y+ = Momentary Switch [package=ksa_sealed_tac_switch]
  Y- = Momentary Switch [package=ksa_sealed_tac_switch]
  Part1 = Arduino Nano (Rev3.0)
  D23 = Diode [package=sma-diode]
  D28 = Diode [package=sma-diode]
  D22 = Diode [package=sma-diode]
  D24 = Diode [package=sma-diode]
  D25 = Diode [package=sma-diode]
  D26 = Diode [package=sma-diode]
  D27 = Diode [package=sma-diode]
  D29 = Diode [package=sma-diode]
  D30 = Diode [package=sma-diode]
  M+ = Momentary Switch [package=ksa_sealed_tac_switch]
  Part4 = Real Time Clock Module - DS1307 RTC Breakout Board from Amazon
  R2 = Resistor [tolerance=±5% resistance=100 package="0402 [SMD]"]
  R1 = Resistor [tolerance=±5% resistance=100 package="0402 [SMD]"]
  R4 = Resistor [tolerance=±5% resistance=100 package="0402 [SMD]"]
  R5 = Resistor [tolerance=±5% resistance=100 package="0402 [SMD]"]
  R6 = Resistor [tolerance=±5% resistance=100 package="0402 [SMD]"]
  R7 = Resistor [tolerance=±5% resistance=100 package="0402 [SMD]"]
  R8 = Resistor [tolerance=±5% resistance=100 package="0402 [SMD]"]
  R9 = Resistor [tolerance=±5% resistance=100 package="0402 [SMD]"]
  R10 = Resistor [tolerance=±5% resistance=100 package="0402 [SMD]"]
  R11 = Resistor [tolerance=±5% resistance=100 package="0402 [SMD]"]
  D31 = Diode [package=sma-diode]
  U1 = EPD connector [package=sod-323]

nets:
  N1: m+.1, m+.2, Part1.A2, D24.A, R4.Pin_0
  VCC: m+.3, m+.4, m-.3, m-.4, h+.3, h+.4, h-.3, h-.4, D+.3, D+.4, D-.3, D-.4, M-.3, M-.4, Y+.3, Y+.4, Y-.3, Y-.4, Part1.5V, M+.3, M+.4, Part4.VCC, U1.VCC
  N2: m-.1, m-.2, Part1.A3, D25.A, R5.Pin_0
  N3: h+.1, h+.2, Part1.A0, D22.A, R1.Pin_0
  N4: h-.1, h-.2, Part1.A1, D23.A, R2.Pin_0
  N5: D+.1, D+.2, Part1.A6, D26.A, R6.Pin_0
  N6: D-.1, D-.2, Part1.A7, D27.A, R7.Pin_0
  N7: M-.1, M-.2, Part1.D5, D29.A, R9.Pin_0
  N8: Y+.1, Y+.2, Part1.D4, D30.A, R10.Pin_0
  N9: Y-.1, Y-.2, Part1.D3, R11.Pin_0, D31.A
  GND: Part1.GND, Part4.GND, R2.Pin_1, R1.Pin_1, R4.Pin_1, R5.Pin_1, R6.Pin_1, R7.Pin_1, R8.Pin_1, R9.Pin_1, R10.Pin_1, R11.Pin_1, U1.GND
  N10: Part1.D2, D23.C, D28.C, D22.C, D24.C, D25.C, D26.C, D27.C, D29.C, D30.C, D31.C
  N11: Part1.D6, D28.A, M+.1, M+.2, R8.Pin_0
  N12: Part1.D7, U1.BUSY
  N13: Part1.D8, U1.RST
  N14: Part1.D9, U1.DC
  N15: Part1.D10, U1.CS
  N16: Part1.D11/MOSI, U1.DIN
  N17: Part1.A5, Part4.SCL
  N18: Part1.A4, Part4.SDA
  N19: Part1.D13/SCK, U1.CLK

custom parts:
  Real Time Clock Module - DS1307 RTC Breakout Board from Amazon: This a custom designed module for the DS1307 Real Time Clock. The module comes fully assembled and pre-programmed with the current time (ok, so it's our current time - MST). The included Lithium coin cell battery (CR1225 41mAh) will run the module for a minimum of 9 years (17 years typical) without external 5V power. The DS1307 is accessed via the I2C protocol. We've written a test-bed to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
  EPD connector: Zener Diode Production Part - 8199 3.4V Zener Voltage
